# Fritzing sketch MusicBox (saved by Fritzing 0.9.3b)
breadboards: 1

parts:
  MusicMaker = Adafruit VS1053 Headphone FeatherWing [part_number="Adafruit #3357"]
  Trellis = Trellis Monochrome Driver PCB for 4x4 Keypad and 3mm LEDs [part_number=1616]
  Left = SPEAKER [package=pcb_mount_speaker]
  Drehencoder = ENCODER_RGB_CA [package=encoder_led_3]
  Right = SPEAKER [package=pcb_mount_speaker]
  Amplifier = Adafruit Stereo 2.1W Class D Audio Amplifier - TPA2012 [part_number="Adafruit #1552"]
  Controller = Adafruit Feather 32u4 Basic Proto [part_number="Adafruit #2771"]
  R1 = Resistor [tolerance=±5% resistance=100k package=THT]

nets:
  N1: MusicMaker.RIGHT_OUT, Amplifier.IN_RIGHT+
  N2: MusicMaker.AGND, Amplifier.IN_RIGHT-, Amplifier.IN_LEFT-
  N3: MusicMaker.LEFT_OUT, Amplifier.IN_LEFT+, Controller.A2
  N4: MusicMaker.MP3RST, Controller.12
  N5: Trellis.INT, Controller.1
  GND: Trellis.GND, Drehencoder.C, Amplifier.GND, Controller.GND, R1.Pin_0
  VCC: Trellis.VCC, Controller.+3V3
  N6: Trellis.SCL, Controller.3
  N7: Trellis.SDA, Controller.2
  N8: Left.+, Amplifier.OUT_LEFT-
  N9: Left.-, Amplifier.OUT_LEFT+
  N10: Drehencoder.-R, Controller.A3
  N11: Drehencoder.-G, Controller.A4
  N12: Drehencoder.SW, Controller.0, R1.Pin_1
  N13: Drehencoder.-B, Controller.A5
  N14: Drehencoder.+, Amplifier.VDD, Controller.VBAT
  N15: Drehencoder.A, Controller.A0
  N16: Drehencoder.B, Controller.A1
  N17: Right.+, Amplifier.OUT_RIGHT-
  N18: Right.-, Amplifier.OUT_RIGHT+
  N19: Amplifier.SHUTDOWN_R, Amplifier.SHUTDOWN_L, Controller.11

notes:
  Direkte Verbindungen von Controller / MusicMaker:
  - Pins 14-16 (MISO,SCLK,MOSI)
  - Pins 5,6,9,10 (Select)
  - 3V3, GND

custom parts:
  Adafruit VS1053 Headphone FeatherWing: Bend all audio files to your will with the Adafruit Music Maker FeatherWing! It's a fun-size version of our Music Maker shield for Arduino! This powerful shield features the VS1053, an encoding/decoding (codec) chip that can decode a wide variety of audio formats such as MP3, AAC, Ogg Vorbis, WMA, MIDI, FLAC, WAV (PCM and ADPCM). You can do all sorts of stuff with the audio as well such as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
  Trellis Monochrome Driver PCB for 4x4 Keypad and 3mm LEDs: Trellis is an open source backlight keypad driver system. It is easy to use, works with any 3mm LEDs and eight tiles can be tiled together on a shared I2C bus. This PCB is specially made to match the Adafruit 4x4 elastomer keypad. Each Trellis PCB has 4x4 pads and 4x4 matching spots for 3mm LEDs. The circuitry on-board handles the background key-presses and LED lighting for the 4x4 tile.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
  Adafruit Stereo 2.1W Class D Audio Amplifier - TPA2012: This incredibly small stereo amplifier is surprisingly powerful - able to deliver 2 x 2.1W channels into 4 ohm impedance speakers (@ 10% THD). Inside the miniature chip is a class D controller, able to run from 2.7V-5.5VDC. Since the amp is a class D, it's incredibly efficient (89% efficient when driving an 8Ω speaker at 1.5 Watt) - making it perfect for portable and battery-powered projects.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
  Adafruit Feather 32u4 Basic Proto: At the Feather 32u4's heart is at ATmega32u4 clocked at 8 MHz and at 3.3V logic, a chip setup we've had tons of experience with as it's the same as the Flora. This chip has 32K of flash and 2K of RAM, with built in USB so not only does it have a USB-to-Serial program & debug capability built in with no need for an FTDI-like chip, it can also act like a mouse, keyboard, USB MIDI device, etc.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
